# Fritzing sketch schematic (saved by Fritzing 0.9.2b)
breadboards: 1

parts:
  Part1 = Arduino Uno (Rev3) - ICSP
  LED1 = LED - 5mm [color="Red (633nm)" package="5 mm [THT]"]
  R1 = Resistor [tolerance=±5% resistance=220 package="2010 [SMD]"]
  LED2 = LED - 5mm [color="Green (565nm)" package="5 mm [THT]"]
  R2 = Resistor [tolerance=±5% resistance=220 package="2010 [SMD]"]
  LED3 = LED - 5mm [color="Blue (525nm)" package="5 mm [THT]"]
  R3 = Resistor [tolerance=±5% resistance=220 package="2010 [SMD]"]
  LED4 = LED - 5mm [color="Yellow (595nm)" package="5 mm [THT]"]
  R4 = Resistor [tolerance=±5% resistance=220 package="2010 [SMD]"]
  S1 = Momentary Switch [package=ksa_sealed_tac_switch]

nets:
  N1: Part1.A0, LED1.anode
  N2: Part1.A1, LED2.anode
  N3: Part1.A2, LED3.anode
  N4: Part1.A3, LED4.anode
  N5: Part1.A5/SCL, S1.1
  N6: Part1.GND, R1.Pin_0, R2.Pin_0, R4.Pin_0, S1.4
  N7: LED1.cathode, R1.Pin_1
  N8: LED2.cathode, R2.Pin_1
  N9: LED3.cathode, R3.Pin_1
  N10: LED4.cathode, R4.Pin_1
